// Logisim project alu.circ as structural Verilog: 1 circuit, main circuit main
module main (
  input  [31:0] X,
  input  [31:0] Y,
  input  [3:0] Switch,
  output Signed_Overflow,
  output Equal,
  output [31:0] Result,
  output [2:0] out,
  output [31:0] out_2,
  output [31:0] out_3,
  output [31:0] out_4
);

  wire adder_3_cout, adder_4_cout, adder_4_out, adder_5_cout, adder_5_out, adder_6_cout, adder_7_cout,
       and_2_out, and_3_out, comparator_2_lt, comparator_3_lt, multiplexer_2_out, multiplexer_4_out,
       or_2_out, or_3_out, or_4_out, or_5_out, overflow0, overflow1, overflow2, overflow3, subtractor_4_bout,
       subtractor_5_bout, subtractor_5_out, subtractor_6_bout, subtractor_6_out, subtractor_7_bout,
       subtractor_8_bout;
  wire [4:0] bit_extender_1_out, bit_extender_2_out, bit_extender_3_out;
  wire [31:0] add, addu, \and , \or , slt, sltu, sub, subu;

  Bit_Extender #(.in_width(32), .out_width(5)) bit_extender_1 (.in(X), .out(bit_extender_1_out));
  Bit_Extender #(.in_width(32), .out_width(5)) bit_extender_2 (.in(X), .out(bit_extender_2_out));
  Bit_Extender #(.in_width(32), .out_width(5)) bit_extender_3 (.in(X), .out(bit_extender_3_out));
  Comparator #(.width(32)) comparator_1 (.a(X), .b(Y), .eq(Equal));  // open: gt, lt
  assign \and  = X & Y;  // AND_Gate and_1, 32 bits wide
  assign \or  = X | Y;  // OR_Gate or_1, 32 bits wide
  Adder #(.width(32)) adder_1 (.a(X), .b(Y), .out(addu), .cout(overflow0));  // open: cin
  Subtractor #(.width(32)) subtractor_1 (.a(X), .b(Y), .out(subu), .bout(overflow1));  // open: bin
  Shifter #(.width(32)) shifter_1 (.in(Y), .\dist (bit_extender_1_out), .out(out_2));
  Shifter #(.width(32), .shift("ar")) shifter_2 (.in(Y), .\dist (bit_extender_2_out), .out(out_3));
  Shifter #(.width(32), .shift("lr")) shifter_3 (.in(Y), .\dist (bit_extender_3_out), .out(out_4));
  Subtractor #(.width(3)) subtractor_2 (.a(Switch[2:0]), .b(3'b001), .out(out));  // open: bin, bout
  Multiplexer #(.select(3), .enable("false")) multiplexer_1 (
    .in0(1'b0), .in1(1'b0), .in2(1'b0), .in3(1'b0), .in4(overflow2), .in5(overflow0), .in6(overflow3),
    .in7(overflow1), .out(Signed_Overflow), .sel(out));
  Comparator #(.width(32), .mode("unsigned")) comparator_2 (.a(X), .b(Y), .lt(comparator_2_lt));  // open: gt, eq
  Adder #(.width(32)) adder_2 (.a(X), .b(Y), .out(add));  // open: cin, cout
  Subtractor #(.width(32)) subtractor_3 (.a(X), .b(Y), .out(sub));  // open: bin, bout
  Multiplexer multiplexer_2 (.in0(1'b0), .in1(1'b1), .out(multiplexer_2_out), .sel(and_2_out));  // open: en
  and and_2 (and_2_out, comparator_2_lt, 1'b1);
  Comparator #(.width(32)) comparator_3 (.a(X), .b(Y), .lt(comparator_3_lt));  // open: gt, eq
  Multiplexer #(.select(4), .width(32)) multiplexer_3 (
    .in0(out_2), .in1(out_4), .in2(out_3), .in3({32{1'b0}}), .in4({32{1'b0}}), .in5(add), .in6(addu),
    .in7(sub), .in8(subu), .in9(\and ), .in10(\or ), .in11(slt), .in12(sltu), .in13({32{1'b0}}),
    .in14({32{1'b0}}), .in15({Y[31:16], {16{1'b0}}}), .out(Result), .sel(Switch));  // open: en
  assign sltu = {{31{1'b0}}, multiplexer_2_out};  // Bit_Extender bit_extender_4
  Multiplexer multiplexer_4 (.in0(1'b0), .in1(1'b1), .out(multiplexer_4_out), .sel(and_3_out));  // open: en
  and and_3 (and_3_out, comparator_3_lt, 1'b1);
  Adder #(.width(30)) adder_3 (.a(X[29:0]), .b(Y[29:0]), .cout(adder_3_cout));  // open: out, cin
  Adder #(.width(1)) adder_4 (.a(X[30]), .b(Y[30]), .out(adder_4_out), .cout(adder_4_cout));  // open: cin
  Adder #(.width(1)) adder_5 (.a(X[31]), .b(Y[31]), .out(adder_5_out), .cout(adder_5_cout));  // open: cin
  Subtractor #(.width(30)) subtractor_4 (.a(X[29:0]), .b(Y[29:0]), .bout(subtractor_4_bout));  // open: out, bin
  Subtractor #(.width(1)) subtractor_5 (
    .a(X[30]), .b(Y[30]), .out(subtractor_5_out), .bout(subtractor_5_bout));  // open: bin
  Subtractor #(.width(1)) subtractor_6 (
    .a(X[31]), .b(Y[31]), .out(subtractor_6_out), .bout(subtractor_6_bout));  // open: bin
  assign slt = {{31{1'b0}}, multiplexer_4_out};  // Bit_Extender bit_extender_5
  Adder #(.width(1)) adder_6 (.a(adder_3_cout), .b(adder_4_out), .cout(adder_6_cout));  // open: out, cin
  Adder #(.width(1)) adder_7 (.a(or_2_out), .b(adder_5_out), .cout(adder_7_cout));  // open: out, cin
  Subtractor #(.width(1)) subtractor_7 (
    .a(subtractor_4_bout), .b(subtractor_5_out), .bout(subtractor_7_bout));  // open: out, bin
  Subtractor #(.width(1)) subtractor_8 (
    .a(or_4_out), .b(subtractor_6_out), .bout(subtractor_8_bout));  // open: out, bin
  or or_2 (or_2_out, adder_6_cout, adder_4_cout);
  or or_3 (or_3_out, adder_7_cout, adder_5_cout);
  or or_4 (or_4_out, subtractor_7_bout, subtractor_5_bout);
  or or_5 (or_5_out, subtractor_8_bout, subtractor_6_bout);
  xor xor_1 (overflow2, or_2_out, or_3_out);
  xor xor_2 (overflow3, or_4_out, or_5_out);

  // Other names for the same wires on the sheet: overflow = Signed_Overflow; S[3:0] = Switch; sll[31:0] = out_2;
  //   sra[31:0] = out_3; srl[31:0] = out_4; lui[31:16] = Y[31:16]

  // Notes on the sheet:
  //   INPUTS to your circuit
  //   DON'T CHANGE THE LOCATIONS OF THE INPUTS AND OUTPUTS!
  //   OUTPUTS from your circuit
endmodule
