// Logisim project cpu.circ as structural Verilog: 1 circuit, main circuit main
module main (
  input  [31:0] INSTRUCTION,
  input  CLOCK,
  output [31:0] FETCH_ADDRESS,
  output [31:0] s0_Value,
  output [31:0] s1_Value,
  output [31:0] s2_Value,
  output [31:0] ra_Value,
  output [31:0] sp_Value,
  output [31:0] swinc,
  output [15:0] Immediate,
  output [3:0] switch,
  output [25:0] inst,
  output swinc_2
);

  wire add, addi, addiu, \and , and_1_out, and_2_out, and_3_out, and_4_out, and_5_out, and_6_out, and_7_out,
       and_8_out, and_9_out, and_10_out, and_11_out, and_12_out, and_13_out, and_14_out, and_15_out,
       and_16_out, and_17_out, and_18_out, and_19_out, and_20_out, and_21_out, and_22_out, and_23_out,
       and_25_out, and_26_out, and_27_out, and_28_out, and_29_out, and_30_out, andi, beq, bnq, boo, Branch,
       comparator_1_eq, comparator_2_eq, comparator_3_eq, comparator_4_eq, comparator_5_eq, comparator_6_eq,
       comparator_7_eq, comparator_8_eq, comparator_9_eq, comparator_10_eq, comparator_11_eq,
       comparator_12_eq, comparator_13_eq, comparator_14_eq, comparator_15_eq, comparator_16_eq,
       comparator_17_eq, comparator_18_eq, comparator_19_eq, comparator_20_eq, comparator_21_eq,
       comparator_22_eq, comparator_23_eq, comparator_24_eq, comparator_25_eq, comparator_26_eq,
       comparator_27_eq, comparator_28_eq, comparator_29_eq, comparator_30_eq, comparator_31_eq,
       comparator_32_eq, comparator_33_eq, comparator_34_eq, comparator_35_eq, comparator_36_eq,
       comparator_37_eq, comparator_38_eq, comparator_39_eq, comparator_40_eq, comparator_41_eq,
       comparator_42_eq, comparator_43_eq, comparator_44_eq, comparator_45_eq, comparator_46_eq,
       comparator_47_eq, comparator_48_eq, comparator_49_eq, comparator_50_eq, comparator_51_eq,
       comparator_52_eq, comparator_53_eq, comparator_54_eq, Equal, Immediate_t, j, jal, jalr, jr, jr_temp,
       Jump, link, lui, lw, main_3_p4, MemWr, NOP, not_1_out, \or , or_1_out, or_7_out, or_8_out, ori,
       overflow, RegDst, RegWr, sll, slt, slti, sltiu, sltu, sra, srl, sub, subu;
  wire [4:0] multiplexer_22_out, multiplexer_23_out;
  wire [5:0] Opcode;
  wire [27:0] adder_1_out;
  wire [31:0] adder_2_out, bit_extender_1_out, bit_extender_2_out, main_1_read_data_1, main_1_read_data_2,
       main_2_result, main_3_p6, multiplexer_4_out, multiplexer_31_out, multiplexer_38_out,
       multiplexer_44_out, multiplexer_51_out, multiplexer_53_out, PC_q, shifter_1_out;
  wire [31:28] adder_1_out_2;

  Multiplexer #(.width(32), .enable("false")) multiplexer_1 (
    .in0(multiplexer_44_out), .in1(swinc), .out(FETCH_ADDRESS), .sel(Jump));
  Comparator #(.width(6)) comparator_1 (.a({6{1'b0}}), .b(Opcode), .eq(comparator_1_eq));  // open: gt, lt
  Comparator #(.width(6)) comparator_2 (.a({6{1'b0}}), .b(Immediate[5:0]), .eq(comparator_2_eq));  // open: gt, lt
  Comparator #(.width(6)) comparator_3 (.a({6{1'b0}}), .b(Opcode), .eq(comparator_3_eq));  // open: gt, lt
  Comparator #(.width(6)) comparator_4 (.a(6'b100001), .b(Immediate[5:0]), .eq(comparator_4_eq));  // open: gt, lt
  Multiplexer #(.enable("false")) multiplexer_2 (.in0(1'b0), .in1(1'b1), .out(\or ), .sel(and_3_out));
  Comparator #(.width(6)) comparator_5 (.a({6{1'b0}}), .b(Opcode), .eq(comparator_5_eq));  // open: gt, lt
  Comparator #(.width(6)) comparator_6 (.a(6'b100101), .b(Immediate[5:0]), .eq(comparator_6_eq));  // open: gt, lt
  Comparator #(.width(6)) comparator_7 (.a(6'b000010), .b(Opcode), .eq(comparator_7_eq));  // open: gt, lt
  Comparator #(.width(6)) comparator_8 (.a({6{1'b0}}), .b(Immediate[5:0]), .eq(comparator_8_eq));  // open: gt, lt
  Comparator #(.width(6)) comparator_9 (.a(6'b001000), .b(Opcode), .eq(comparator_9_eq));  // open: gt, lt
  Comparator #(.width(6)) comparator_10 (.a({6{1'b0}}), .b(Immediate[5:0]), .eq(comparator_10_eq));  // open: gt, lt
  Multiplexer #(.width(32), .enable("false")) multiplexer_3 (
    .in0({adder_1_out_2, inst[25:16], Immediate, 2'b00}), .in1(main_1_read_data_1), .out(swinc), .sel(jr_temp));
  Register #(.width(32)) PC (.D(FETCH_ADDRESS), .Q(PC_q), .clk(CLOCK));  // open: en, clr
  Multiplexer #(.width(32), .enable("false")) multiplexer_4 (
    .in0(INSTRUCTION), .in1({32{1'b0}}), .out(multiplexer_4_out), .sel(NOP));
  Multiplexer #(.enable("false")) multiplexer_5 (.in0(1'b0), .in1(1'b1), .out(sll), .sel(and_2_out));
  Multiplexer #(.enable("false")) multiplexer_6 (.in0(1'b0), .in1(1'b1), .out(addi), .sel(and_1_out));
  and and_1 (and_1_out, comparator_3_eq, comparator_4_eq);
  Comparator #(.width(6)) comparator_11 (.a(6'b000100), .b(Opcode), .eq(comparator_11_eq));  // open: gt, lt
  Comparator #(.width(6)) comparator_12 (.a({6{1'b0}}), .b(Immediate[5:0]), .eq(comparator_12_eq));  // open: gt, lt
  Comparator #(.width(6)) comparator_13 (.a(6'b001010), .b(Opcode), .eq(comparator_13_eq));  // open: gt, lt
  Comparator #(.width(6)) comparator_14 (.a({6{1'b0}}), .b(Immediate[5:0]), .eq(comparator_14_eq));  // open: gt, lt
  Comparator #(.width(6)) comparator_15 (.a(6'b001010), .b(Opcode), .eq(comparator_15_eq));  // open: gt, lt
  Comparator #(.width(6)) comparator_16 (.a({6{1'b0}}), .b(Immediate[5:0]), .eq(comparator_16_eq));  // open: gt, lt
  Adder #(.width(32)) adder_1 (.a(32'h4), .b(PC_q), .out({adder_1_out_2, adder_1_out}));  // open: cin, cout
  Register #(.width(32)) register_1 (
    .D(multiplexer_4_out), .Q({Opcode, inst[25:16], Immediate}), .clk(CLOCK));  // open: en, clr
  Multiplexer #(.width(4), .enable("false")) multiplexer_7 (.in1(4'b0000), .out(switch), .sel(and_2_out));  // open: in0
  and and_2 (and_2_out, comparator_1_eq, comparator_2_eq);
  Multiplexer #(.width(4), .enable("false")) multiplexer_8 (.in1(4'b0110), .out(switch), .sel(and_1_out));  // open: in0
  Multiplexer #(.width(4), .enable("false")) multiplexer_9 (.in1(4'b1010), .out(switch), .sel(and_3_out));  // open: in0
  and and_3 (and_3_out, comparator_5_eq, comparator_6_eq);
  Multiplexer #(.enable("false")) multiplexer_10 (.in0(1'b0), .in1(1'b1), .out(j), .sel(and_4_out));
  and and_4 (and_4_out, comparator_7_eq, comparator_8_eq);
  Multiplexer #(.enable("false")) multiplexer_11 (.in0(1'b0), .in1(1'b1), .out(beq), .sel(and_5_out));
  and and_5 (and_5_out, comparator_11_eq, comparator_12_eq);
  Multiplexer #(.enable("false")) multiplexer_12 (.in0(1'b0), .in1(1'b1), .out(addi), .sel(and_6_out));
  Multiplexer #(.width(4), .enable("false")) multiplexer_13 (
    .in1(4'b0101), .out(switch), .sel(and_6_out));  // open: in0
  and and_6 (and_6_out, comparator_9_eq, comparator_10_eq);
  Multiplexer #(.enable("false")) multiplexer_14 (.in0(1'b0), .in1(1'b1), .out(slti), .sel(and_7_out));
  and and_7 (and_7_out, comparator_13_eq, comparator_14_eq);
  Multiplexer #(.width(4), .enable("false")) multiplexer_15 (
    .in1(4'b0101), .out(switch), .sel(and_8_out));  // open: in0
  and and_8 (and_8_out, comparator_15_eq, comparator_16_eq);
  Multiplexer #(.width(4), .enable("false")) multiplexer_16 (
    .in1(4'b1011), .out(switch), .sel(and_7_out));  // open: in0
  Multiplexer #(.enable("false")) multiplexer_17 (.in0(1'b0), .in1(1'b1), .out(lw), .sel(and_8_out));
  Multiplexer #(.enable("false")) multiplexer_18 (.in0(1'b0), .in1(1'b1), .out(srl), .sel(and_9_out));
  Comparator #(.width(6)) comparator_17 (.a({6{1'b0}}), .b(Opcode), .eq(comparator_17_eq));  // open: gt, lt
  Comparator #(.width(6)) comparator_18 (.a(6'b000010), .b(Immediate[5:0]), .eq(comparator_18_eq));  // open: gt, lt
  Multiplexer #(.enable("false")) multiplexer_19 (.in0(1'b0), .in1(1'b1), .out(sub), .sel(and_10_out));
  Comparator #(.width(6)) comparator_19 (.a({6{1'b0}}), .b(Opcode), .eq(comparator_19_eq));  // open: gt, lt
  Comparator #(.width(6)) comparator_20 (.a(6'b100010), .b(Immediate[5:0]), .eq(comparator_20_eq));  // open: gt, lt
  Comparator #(.width(6)) comparator_21 (.a({6{1'b0}}), .b(Opcode), .eq(comparator_21_eq));  // open: gt, lt
  Comparator #(.width(6)) comparator_22 (.a(6'b101010), .b(Immediate[5:0]), .eq(comparator_22_eq));  // open: gt, lt
  Comparator #(.width(6)) comparator_23 (.a(6'b000011), .b(Opcode), .eq(comparator_23_eq));  // open: gt, lt
  Comparator #(.width(6)) comparator_24 (.a({6{1'b0}}), .b(Immediate[5:0]), .eq(comparator_24_eq));  // open: gt, lt
  Comparator #(.width(6)) comparator_25 (.a(6'b000101), .b(Opcode), .eq(comparator_25_eq));  // open: gt, lt
  Comparator #(.width(6)) comparator_26 (.a({6{1'b0}}), .b(Immediate[5:0]), .eq(comparator_26_eq));  // open: gt, lt
  Comparator #(.width(6)) comparator_27 (.a(6'b001001), .b(Opcode), .eq(comparator_27_eq));  // open: gt, lt
  Comparator #(.width(6)) comparator_28 (.a({6{1'b0}}), .b(Immediate[5:0]), .eq(comparator_28_eq));  // open: gt, lt
  and and_9 (and_9_out, comparator_17_eq, comparator_18_eq);
  and and_10 (and_10_out, comparator_19_eq, comparator_20_eq);
  Multiplexer #(.enable("false")) multiplexer_20 (.in0(1'b0), .in1(1'b1), .out(slt), .sel(and_11_out));
  and and_11 (and_11_out, comparator_21_eq, comparator_22_eq);
  and and_12 (and_12_out, comparator_23_eq, comparator_24_eq);
  Multiplexer #(.enable("false")) multiplexer_21 (.in0(1'b0), .in1(1'b1), .out(addiu), .sel(and_13_out));
  and and_13 (and_13_out, comparator_27_eq, comparator_28_eq);
  Comparator #(.width(6)) comparator_29 (.a(6'b001011), .b(Opcode), .eq(comparator_29_eq));  // open: gt, lt
  Comparator #(.width(6)) comparator_30 (.a({6{1'b0}}), .b(Immediate[5:0]), .eq(comparator_30_eq));  // open: gt, lt
  Comparator #(.width(6)) comparator_31 (.a(6'b001111), .b(Opcode), .eq(comparator_31_eq));  // open: gt, lt
  Comparator #(.width(6)) comparator_32 (.a({6{1'b0}}), .b(Immediate[5:0]), .eq(comparator_32_eq));  // open: gt, lt
  Multiplexer #(.width(5), .enable("false")) multiplexer_22 (
    .in0(multiplexer_23_out), .in1({5{1'b1}}), .out(multiplexer_22_out), .sel(link));
  Multiplexer #(.width(5), .enable("false")) multiplexer_23 (
    .in0(inst[20:16]), .in1(Immediate[15:11]), .out(multiplexer_23_out), .sel(RegDst));
  assign bit_extender_1_out = {{16{1'b0}}, Immediate};  // Bit_Extender bit_extender_1
  assign bit_extender_2_out = {{16{Immediate[15]}}, Immediate};  // Bit_Extender bit_extender_2
  Multiplexer #(.width(4), .enable("false")) multiplexer_24 (
    .in1(4'b0001), .out(switch), .sel(and_9_out));  // open: in0
  Multiplexer #(.width(4), .enable("false")) multiplexer_25 (
    .in1(4'b0111), .out(switch), .sel(and_10_out));  // open: in0
  Multiplexer #(.width(4), .enable("false")) multiplexer_26 (
    .in1(4'b1011), .out(switch), .sel(and_11_out));  // open: in0
  Multiplexer #(.enable("false")) multiplexer_27 (.in0(1'b0), .in1(1'b1), .out(jal), .sel(and_12_out));
  Multiplexer #(.enable("false")) multiplexer_28 (.in0(1'b0), .in1(1'b1), .out(bnq), .sel(and_14_out));
  and and_14 (and_14_out, comparator_25_eq, comparator_26_eq);
  Multiplexer #(.width(4), .enable("false")) multiplexer_29 (
    .in1(4'b0110), .out(switch), .sel(and_13_out));  // open: in0
  Multiplexer #(.width(4), .enable("false")) multiplexer_30 (
    .in1(4'b1111), .out(switch), .sel(and_15_out));  // open: in0
  and and_15 (and_15_out, comparator_31_eq, comparator_32_eq);
  Shifter #(.width(32)) shifter_1 (.in(multiplexer_31_out), .\dist (5'b00010), .out(shifter_1_out));
  Multiplexer #(.width(32), .enable("false")) multiplexer_31 (
    .in0(bit_extender_1_out), .in1(bit_extender_2_out), .out(multiplexer_31_out), .sel(swinc_2));
  Comparator #(.width(6)) comparator_33 (.a({6{1'b0}}), .b(Opcode), .eq(comparator_33_eq));  // open: gt, lt
  Comparator #(.width(6)) comparator_34 (.a(6'b100011), .b(Immediate[5:0]), .eq(comparator_34_eq));  // open: gt, lt
  Multiplexer #(.enable("false")) multiplexer_32 (.in0(1'b0), .in1(1'b1), .out(sltiu), .sel(and_16_out));
  Multiplexer #(.width(4), .enable("false")) multiplexer_33 (
    .in1(4'b1100), .out(switch), .sel(and_16_out));  // open: in0
  and and_16 (and_16_out, comparator_29_eq, comparator_30_eq);
  Multiplexer #(.enable("false")) multiplexer_34 (.in0(1'b0), .in1(1'b1), .out(lui), .sel(and_15_out));
  regfile_main main_1 (
    .Read_Register_1(inst[25:21]), .Read_Register_2(inst[20:16]), .Write_Register(multiplexer_22_out),
    .Write_Data(multiplexer_51_out), .Write_Enable(RegWr), .Clock(CLOCK), .Read_Data_1(main_1_read_data_1),
    .Read_Data_2(main_1_read_data_2), .s0_Value(s0_Value), .s1_Value(s1_Value), .s2_Value(s2_Value),
    .ra_Value(ra_Value), .sp_Value(sp_Value));
  Multiplexer #(.enable("false")) multiplexer_35 (.in0(1'b0), .in1(1'b1), .out(sra), .sel(and_17_out));
  Comparator #(.width(6)) comparator_35 (.a({6{1'b0}}), .b(Opcode), .eq(comparator_35_eq));  // open: gt, lt
  Comparator #(.width(6)) comparator_36 (.a(6'b000011), .b(Immediate[5:0]), .eq(comparator_36_eq));  // open: gt, lt
  Multiplexer #(.enable("false")) multiplexer_36 (.in0(1'b0), .in1(1'b1), .out(subu), .sel(and_18_out));
  Multiplexer #(.enable("false")) multiplexer_37 (.in0(1'b0), .in1(1'b1), .out(sltu), .sel(and_19_out));
  Comparator #(.width(6)) comparator_37 (.a({6{1'b0}}), .b(Opcode), .eq(comparator_37_eq));  // open: gt, lt
  Comparator #(.width(6)) comparator_38 (.a(6'b101011), .b(Immediate[5:0]), .eq(comparator_38_eq));  // open: gt, lt
  Comparator #(.width(6)) comparator_39 (.a({6{1'b0}}), .b(Opcode), .eq(comparator_39_eq));  // open: gt, lt
  Comparator #(.width(6)) comparator_40 (.a(6'b001000), .b(Immediate[5:0]), .eq(comparator_40_eq));  // open: gt, lt
  Comparator #(.width(6)) comparator_41 (.a(6'b000110), .b(Opcode), .eq(comparator_41_eq));  // open: gt, lt
  Comparator #(.width(6)) comparator_42 (.a({6{1'b0}}), .b(Immediate[5:0]), .eq(comparator_42_eq));  // open: gt, lt
  Comparator #(.width(6)) comparator_43 (.a(6'b001100), .b(Opcode), .eq(comparator_43_eq));  // open: gt, lt
  Comparator #(.width(6)) comparator_44 (.a({6{1'b0}}), .b(Immediate[5:0]), .eq(comparator_44_eq));  // open: gt, lt
  Adder #(.width(32)) adder_2 (
    .a({adder_1_out_2, adder_1_out}), .b(shifter_1_out), .out(adder_2_out));  // open: cin, cout
  LED led_1 (.in(overflow));
  alu_main main_2 (
    .Switch(switch), .X(main_1_read_data_1), .Equal(Equal), .Result(main_2_result),
    .Signed_Overflow(overflow), .Y(multiplexer_38_out));  // open: out_2, out_3, out_4, out
  Multiplexer #(.width(32), .enable("false")) multiplexer_38 (
    .in0(main_1_read_data_2), .in1(multiplexer_31_out), .out(multiplexer_38_out), .sel(Immediate_t));
  Multiplexer #(.width(4), .enable("false")) multiplexer_39 (
    .in1(4'b0010), .out(switch), .sel(and_17_out));  // open: in0
  and and_17 (and_17_out, comparator_35_eq, comparator_36_eq);
  Multiplexer #(.width(4), .enable("false")) multiplexer_40 (
    .in1(4'b1000), .out(switch), .sel(and_18_out));  // open: in0
  and and_18 (and_18_out, comparator_33_eq, comparator_34_eq);
  Multiplexer #(.width(4), .enable("false")) multiplexer_41 (
    .in1(4'b1100), .out(switch), .sel(and_19_out));  // open: in0
  and and_19 (and_19_out, comparator_37_eq, comparator_38_eq);
  Multiplexer #(.enable("false")) multiplexer_42 (.in0(1'b0), .in1(1'b1), .out(jr), .sel(and_20_out));
  and and_20 (and_20_out, comparator_39_eq, comparator_40_eq);
  and and_21 (and_21_out, comparator_41_eq, comparator_42_eq);
  Multiplexer #(.enable("false")) multiplexer_43 (.in0(1'b0), .in1(1'b1), .out(andi), .sel(and_22_out));
  and and_22 (and_22_out, comparator_43_eq, comparator_44_eq);
  Comparator #(.width(6)) comparator_45 (.a(6'b101011), .b(Opcode), .eq(comparator_45_eq));  // open: gt, lt
  Comparator #(.width(6)) comparator_46 (.a({6{1'b0}}), .b(Immediate[5:0]), .eq(comparator_46_eq));  // open: gt, lt
  Multiplexer #(.width(32), .enable("false")) multiplexer_44 (
    .in0({adder_1_out_2, adder_1_out}), .in1(adder_2_out), .out(multiplexer_44_out), .sel(Branch));
  Multiplexer #(.enable("false")) multiplexer_45 (.in0(1'b0), .in1(1'b1), .out(boo), .sel(and_21_out));
  Multiplexer #(.width(4), .enable("false")) multiplexer_46 (
    .in1(4'b1001), .out(switch), .sel(and_22_out));  // open: in0
  Multiplexer #(.width(4), .enable("false")) multiplexer_47 (
    .in1(4'b0101), .out(switch), .sel(and_23_out));  // open: in0
  and and_23 (and_23_out, comparator_45_eq, comparator_46_eq);
  Multiplexer #(.enable("false")) multiplexer_48 (.in0(1'b0), .in1(1'b1), .out(add), .sel(main_3_p4));
  Comparator #(.width(6)) comparator_47 (.a({6{1'b0}}), .b(Opcode), .eq(comparator_47_eq));  // open: gt, lt
  Comparator #(.width(6)) comparator_48 (.a(6'b100000), .b(Immediate[5:0]), .eq(comparator_48_eq));  // open: gt, lt
  Multiplexer #(.enable("false")) multiplexer_49 (.in0(1'b0), .in1(1'b1), .out(\and ), .sel(and_25_out));
  Comparator #(.width(6)) comparator_49 (.a({6{1'b0}}), .b(Opcode), .eq(comparator_49_eq));  // open: gt, lt
  Comparator #(.width(6)) comparator_50 (.a(6'b100100), .b(Immediate[5:0]), .eq(comparator_50_eq));  // open: gt, lt
  Comparator #(.width(6)) comparator_51 (.a({6{1'b0}}), .b(Opcode), .eq(comparator_51_eq));  // open: gt, lt
  Comparator #(.width(6)) comparator_52 (.a(6'b001001), .b(Immediate[5:0]), .eq(comparator_52_eq));  // open: gt, lt
  Multiplexer #(.enable("false")) multiplexer_50 (.in0(1'b0), .in1(1'b1), .out(MemWr), .sel(and_23_out));
  // mem_main main_3: pin names not known; wires that end beside it: main_2_result, main_1_read_data_2, MemWr, main_3_p4, CLOCK, main_3_p6
  Multiplexer #(.width(32)) multiplexer_51 (
    .in0(multiplexer_53_out), .in1({adder_1_out_2, adder_1_out}), .out(multiplexer_51_out), .en(link));  // open: sel
  and and_24 (main_3_p4, comparator_47_eq, comparator_48_eq);
  Multiplexer #(.width(4), .enable("false")) multiplexer_52 (
    .in1(4'b1001), .out(switch), .sel(and_25_out));  // open: in0
  and and_25 (and_25_out, comparator_49_eq, comparator_50_eq);
  and and_26 (and_26_out, comparator_51_eq, comparator_52_eq);
  Comparator #(.width(6)) comparator_53 (.a(6'b001101), .b(Opcode), .eq(comparator_53_eq));  // open: gt, lt
  Comparator #(.width(6)) comparator_54 (.a({6{1'b0}}), .b(Immediate[5:0]), .eq(comparator_54_eq));  // open: gt, lt
  Multiplexer #(.width(32), .disabled(0), .enable("false")) multiplexer_53 (
    .in0(main_2_result), .in1(main_3_p6), .out(multiplexer_53_out), .sel(lw));
  Multiplexer #(.width(4), .enable("false")) multiplexer_54 (
    .in1(4'b0101), .out(switch), .sel(main_3_p4));  // open: in0
  Multiplexer #(.enable("false")) multiplexer_55 (.in0(1'b0), .in1(1'b1), .out(jalr), .sel(and_26_out));
  Multiplexer #(.enable("false")) multiplexer_56 (.in0(1'b0), .in1(1'b1), .out(ori), .sel(and_27_out));
  and and_27 (and_27_out, comparator_53_eq, comparator_54_eq);
  Multiplexer #(.width(4), .enable("false")) multiplexer_57 (
    .in1(4'b1010), .out(switch), .sel(and_27_out));  // open: in0
  and and_28 (and_28_out, Equal, beq);
  not not_1 (not_1_out, Equal);
  and and_29 (and_29_out, overflow, boo);
  and and_30 (and_30_out, not_1_out, bnq);
  Multiplexer #(.enable("false")) multiplexer_58 (.in0(1'b0), .in1(1'b1), .out(NOP), .sel(or_1_out));
  or or_1 (or_1_out, Branch, Jump);
  or or_2 (swinc_2, addiu, sltiu, slti, addi);
  or or_3 (Immediate_t, ori, andi, sltiu, slti, addiu, addi);
  or or_4 (link, jal, jalr);
  or or_5 (Branch, and_28_out, and_30_out, and_29_out);
  or or_6 (Jump, j, jal, jr, jalr);
  or or_7 (or_7_out, MemWr, beq, bnq, boo, j, jr);
  not not_2 (RegDst, or_8_out);
  or or_8 (or_8_out, ori, andi, sltiu, slti, addiu, addi);
  or or_9 (jr_temp, jr, jalr);
  not not_3 (RegWr, or_7_out);

  assign inst[15:0] = Immediate;

  // Other names for the same wires on the sheet: clk = CLOCK; fetch_addr[31:0] = FETCH_ADDRESS;
  //   Funct[5:0] = Immediate[5:0]; MemToReg = lw; ra[31:0] = ra_Value; s0[31:0] = s0_Value; s1[31:0] = s1_Value;
  //   s2[31:0] = s2_Value; SignExt = swinc_2; sp[31:0] = sp_Value; sw = MemWr

  // Notes on the sheet:
  //   addu
  //   or
  //   sll
  //   j
  //   beq
  //   addi
  //   slti
  //   Output
  //   lw
  //   These are outputs/inputs from run.circ
  //   Inputs
  //   srl
  //   sub
  //   jal
  //   slt
  //   bnq
  //   addiu
  //   sltiu
  //   lui
  //   sra
  //   subu
  //   sltu
  //   jr
  //   andi
  //   boo
  //   These are DEBUG/TEST outputs from your circuit.
  //   sw
  //   and
  //    jalr
  //   add
  //   ori
  //   jump kind of things need further clarification.
endmodule
