// Logisim project regfile.circ as structural Verilog: 1 circuit, main circuit main
module main (
  input  [4:0] Read_Register_1,
  input  [4:0] Read_Register_2,
  input  [4:0] Write_Register,
  input  [31:0] Write_Data,
  input  Write_Enable,
  input  Clock,
  output [31:0] s0_Value,
  output [31:0] s1_Value,
  output [31:0] s2_Value,
  output [31:0] ra_Value,
  output [31:0] sp_Value,
  output [31:0] Read_Data_1,
  output [31:0] Read_Data_2
);

  wire comparator_1_eq, comparator_2_eq, comparator_3_eq, comparator_4_eq, comparator_5_eq, comparator_6_eq,
       comparator_7_eq, comparator_8_eq, comparator_9_eq, comparator_10_eq, comparator_11_eq,
       comparator_12_eq, comparator_13_eq, comparator_14_eq, comparator_15_eq, comparator_16_eq,
       comparator_17_eq, comparator_18_eq, comparator_19_eq, comparator_20_eq, comparator_21_eq,
       comparator_22_eq, comparator_23_eq, comparator_24_eq, comparator_25_eq, comparator_26_eq,
       comparator_27_eq, comparator_28_eq, comparator_29_eq, comparator_30_eq, comparator_31_eq,
       comparator_32_eq, comparator_33_eq, comparator_34_eq, comparator_35_eq, comparator_36_eq,
       comparator_37_eq, comparator_38_eq, comparator_39_eq, comparator_40_eq, comparator_41_eq,
       comparator_42_eq, comparator_43_eq, comparator_44_eq, comparator_45_eq, comparator_46_eq,
       comparator_47_eq, comparator_48_eq, comparator_49_eq, comparator_50_eq, comparator_51_eq,
       comparator_52_eq, comparator_53_eq, comparator_54_eq, comparator_55_eq, comparator_56_eq,
       comparator_57_eq, comparator_58_eq, comparator_59_eq, comparator_60_eq, comparator_61_eq,
       comparator_62_eq, comparator_63_eq, comparator_64_eq, comparator_65_eq, comparator_66_eq,
       comparator_67_eq, comparator_68_eq, comparator_69_eq, comparator_70_eq, comparator_71_eq,
       comparator_72_eq, comparator_73_eq, comparator_74_eq, comparator_75_eq, comparator_76_eq,
       comparator_77_eq, comparator_78_eq, comparator_79_eq, comparator_80_eq, comparator_81_eq,
       comparator_82_eq, comparator_83_eq, comparator_84_eq, comparator_85_eq, comparator_86_eq,
       comparator_87_eq, comparator_88_eq, comparator_89_eq, comparator_90_eq, comparator_91_eq,
       comparator_92_eq, comparator_93_eq, comparator_94_eq, comparator_95_eq;
  wire [4:0] multiplexer_1_out, multiplexer_2_out, multiplexer_3_out, multiplexer_4_out, multiplexer_5_out,
       multiplexer_6_out, multiplexer_7_out, multiplexer_8_out, multiplexer_9_out, multiplexer_10_out,
       multiplexer_11_out, multiplexer_12_out, multiplexer_13_out, multiplexer_14_out, multiplexer_15_out,
       multiplexer_63_out, multiplexer_64_out, multiplexer_65_out, multiplexer_66_out, multiplexer_67_out,
       multiplexer_68_out, multiplexer_69_out, multiplexer_70_out, multiplexer_71_out, multiplexer_72_out,
       multiplexer_73_out, multiplexer_74_out, multiplexer_75_out, multiplexer_76_out, multiplexer_77_out,
       multiplexer_78_out;
  wire [31:0] multiplexer_16_out, multiplexer_17_out, multiplexer_18_out, multiplexer_19_out,
       multiplexer_20_out, multiplexer_21_out, multiplexer_22_out, multiplexer_23_out, multiplexer_24_out,
       multiplexer_25_out, multiplexer_26_out, multiplexer_27_out, multiplexer_28_out, multiplexer_29_out,
       multiplexer_30_out, multiplexer_79_out, multiplexer_80_out, multiplexer_81_out, multiplexer_82_out,
       multiplexer_83_out, multiplexer_84_out, multiplexer_85_out, multiplexer_86_out, multiplexer_87_out,
       multiplexer_88_out, multiplexer_89_out, multiplexer_90_out, multiplexer_91_out, multiplexer_92_out,
       multiplexer_93_out, multiplexer_94_out, register_1_q, register_2_q, register_3_q, register_4_q,
       register_5_q, register_6_q, register_7_q, register_8_q, register_9_q, register_10_q, register_11_q,
       register_12_q, register_13_q, register_14_q, register_17_q, register_18_q, register_19_q,
       register_20_q, register_22_q, register_23_q, register_24_q, register_25_q, register_26_q,
       register_29_q, register_30_q, register_31_q, register_32_q;

  Multiplexer #(.width(5), .enable("false")) multiplexer_1 (
    .in1(Write_Register), .out(multiplexer_1_out), .sel(Write_Enable));  // open: in0
  Multiplexer #(.width(5), .enable("false")) multiplexer_2 (
    .in1(Write_Register), .out(multiplexer_2_out), .sel(Write_Enable));  // open: in0
  Multiplexer #(.width(5), .enable("false")) multiplexer_3 (
    .in1(Write_Register), .out(multiplexer_3_out), .sel(Write_Enable));  // open: in0
  Multiplexer #(.width(5), .enable("false")) multiplexer_4 (
    .in1(Write_Register), .out(multiplexer_4_out), .sel(Write_Enable));  // open: in0
  Multiplexer #(.width(5), .enable("false")) multiplexer_5 (
    .in1(Write_Register), .out(multiplexer_5_out), .sel(Write_Enable));  // open: in0
  Multiplexer #(.width(5), .enable("false")) multiplexer_6 (
    .in1(Write_Register), .out(multiplexer_6_out), .sel(Write_Enable));  // open: in0
  Multiplexer #(.width(5), .enable("false")) multiplexer_7 (
    .in1(Write_Register), .out(multiplexer_7_out), .sel(Write_Enable));  // open: in0
  Multiplexer #(.width(5), .enable("false")) multiplexer_8 (
    .in1(Write_Register), .out(multiplexer_8_out), .sel(Write_Enable));  // open: in0
  Multiplexer #(.width(5), .enable("false")) multiplexer_9 (
    .in1(Write_Register), .out(multiplexer_9_out), .sel(Write_Enable));  // open: in0
  Multiplexer #(.width(5), .enable("false")) multiplexer_10 (
    .in1(Write_Register), .out(multiplexer_10_out), .sel(Write_Enable));  // open: in0
  Multiplexer #(.width(5), .enable("false")) multiplexer_11 (
    .in1(Write_Register), .out(multiplexer_11_out), .sel(Write_Enable));  // open: in0
  Multiplexer #(.width(5), .enable("false")) multiplexer_12 (
    .in1(Write_Register), .out(multiplexer_12_out), .sel(Write_Enable));  // open: in0
  Multiplexer #(.width(5), .enable("false")) multiplexer_13 (
    .in1(Write_Register), .out(multiplexer_13_out), .sel(Write_Enable));  // open: in0
  Multiplexer #(.width(5), .enable("false")) multiplexer_14 (
    .in1(Write_Register), .out(multiplexer_14_out), .sel(Write_Enable));  // open: in0
  Multiplexer #(.width(5), .enable("false")) multiplexer_15 (
    .in1(Write_Register), .out(multiplexer_15_out), .sel(Write_Enable));  // open: in0
  Comparator #(.width(5)) comparator_1 (.a(5'b01000), .b(multiplexer_1_out), .eq(comparator_1_eq));  // open: gt, lt
  Comparator #(.width(5)) comparator_2 (.a(5'b01010), .b(multiplexer_2_out), .eq(comparator_2_eq));  // open: gt, lt
  Comparator #(.width(5)) comparator_3 (.a(5'b01100), .b(multiplexer_3_out), .eq(comparator_3_eq));  // open: gt, lt
  Multiplexer #(.width(32), .enable("false")) multiplexer_16 (
    .in1(Write_Data), .out(multiplexer_16_out), .sel(comparator_4_eq));  // open: in0
  Comparator #(.width(5)) comparator_4 (.a(5'b01110), .b(multiplexer_4_out), .eq(comparator_4_eq));  // open: gt, lt
  Comparator #(.width(5)) comparator_5 (.a(5'b10000), .b(multiplexer_5_out), .eq(comparator_5_eq));  // open: gt, lt
  Comparator #(.width(5)) comparator_6 (.a(5'b10010), .b(multiplexer_6_out), .eq(comparator_6_eq));  // open: gt, lt
  Multiplexer #(.width(32), .enable("false")) multiplexer_17 (
    .in1(Write_Data), .out(multiplexer_17_out), .sel(comparator_7_eq));  // open: in0
  Comparator #(.width(5)) comparator_7 (.a(5'b10100), .b(multiplexer_7_out), .eq(comparator_7_eq));  // open: gt, lt
  Multiplexer #(.width(32), .enable("false")) multiplexer_18 (
    .in1(Write_Data), .out(multiplexer_18_out), .sel(comparator_8_eq));  // open: in0
  Comparator #(.width(5)) comparator_8 (.a(5'b10110), .b(multiplexer_8_out), .eq(comparator_8_eq));  // open: gt, lt
  Comparator #(.width(5)) comparator_9 (.a(5'b11000), .b(multiplexer_9_out), .eq(comparator_9_eq));  // open: gt, lt
  Comparator #(.width(5)) comparator_10 (.a(5'b11010), .b(multiplexer_10_out), .eq(comparator_10_eq));  // open: gt, lt
  Multiplexer #(.width(32), .enable("false")) multiplexer_19 (
    .in1(Write_Data), .out(multiplexer_19_out), .sel(comparator_11_eq));  // open: in0
  Comparator #(.width(5)) comparator_11 (.a(5'b11100), .b(multiplexer_11_out), .eq(comparator_11_eq));  // open: gt, lt
  Multiplexer #(.width(32), .enable("false")) multiplexer_20 (
    .in1(Write_Data), .out(multiplexer_20_out), .sel(comparator_12_eq));  // open: in0
  Comparator #(.width(5)) comparator_12 (.a(5'b11110), .b(multiplexer_12_out), .eq(comparator_12_eq));  // open: gt, lt
  Multiplexer #(.width(32), .enable("false")) multiplexer_21 (
    .in1(Write_Data), .out(multiplexer_21_out), .sel(comparator_13_eq));  // open: in0
  Comparator #(.width(5)) comparator_13 (.a(5'b00010), .b(multiplexer_13_out), .eq(comparator_13_eq));  // open: gt, lt
  Multiplexer #(.width(32), .enable("false")) multiplexer_22 (
    .in1(Write_Data), .out(multiplexer_22_out), .sel(comparator_14_eq));  // open: in0
  Comparator #(.width(5)) comparator_14 (.a(5'b00100), .b(multiplexer_14_out), .eq(comparator_14_eq));  // open: gt, lt
  Multiplexer #(.width(32), .enable("false")) multiplexer_23 (
    .in1(Write_Data), .out(multiplexer_23_out), .sel(comparator_15_eq));  // open: in0
  Comparator #(.width(5)) comparator_15 (.a(5'b00110), .b(multiplexer_15_out), .eq(comparator_15_eq));  // open: gt, lt
  Multiplexer #(.width(32), .enable("false")) multiplexer_24 (
    .in1(Write_Data), .out(multiplexer_24_out), .sel(comparator_1_eq));  // open: in0
  Multiplexer #(.width(32), .enable("false")) multiplexer_25 (
    .in1(Write_Data), .out(multiplexer_25_out), .sel(comparator_2_eq));  // open: in0
  Multiplexer #(.width(32), .enable("false")) multiplexer_26 (
    .in1(Write_Data), .out(multiplexer_26_out), .sel(comparator_3_eq));  // open: in0
  Register #(.width(32)) register_1 (.D(multiplexer_26_out), .Q(register_1_q), .clk(Clock));  // open: en, clr
  Register #(.width(32)) register_2 (.D(multiplexer_16_out), .Q(register_2_q), .clk(Clock));  // open: en, clr
  Multiplexer #(.width(32), .enable("false")) multiplexer_27 (
    .in1(Write_Data), .out(multiplexer_27_out), .sel(comparator_5_eq));  // open: in0
  Multiplexer #(.width(32), .enable("false")) multiplexer_28 (
    .in1(Write_Data), .out(multiplexer_28_out), .sel(comparator_6_eq));  // open: in0
  Register #(.width(32)) register_3 (.D(multiplexer_17_out), .Q(register_3_q), .clk(Clock));  // open: en, clr
  Register #(.width(32)) register_4 (.D(multiplexer_18_out), .Q(register_4_q), .clk(Clock));  // open: en, clr
  Multiplexer #(.width(32), .enable("false")) multiplexer_29 (
    .in1(Write_Data), .out(multiplexer_29_out), .sel(comparator_9_eq));  // open: in0
  Register #(.width(32)) register_5 (.D(multiplexer_29_out), .Q(register_5_q), .clk(Clock));  // open: en, clr
  Multiplexer #(.width(32), .enable("false")) multiplexer_30 (
    .in1(Write_Data), .out(multiplexer_30_out), .sel(comparator_10_eq));  // open: in0
  Register #(.width(32)) register_6 (.D(multiplexer_30_out), .Q(register_6_q), .clk(Clock));  // open: en, clr
  Register #(.width(32)) register_7 (.D(multiplexer_19_out), .Q(register_7_q), .clk(Clock));  // open: en, clr
  Register #(.width(32)) register_8 (.D(multiplexer_20_out), .Q(register_8_q), .clk(Clock));  // open: en, clr
  Register #(.width(32)) register_9 (.Q(register_9_q), .clk(Clock));  // open: D, en, clr
  Register #(.width(32)) register_10 (.D(multiplexer_21_out), .Q(register_10_q), .clk(Clock));  // open: en, clr
  Register #(.width(32)) register_11 (.D(multiplexer_22_out), .Q(register_11_q), .clk(Clock));  // open: en, clr
  Register #(.width(32)) register_12 (.D(multiplexer_23_out), .Q(register_12_q), .clk(Clock));  // open: en, clr
  Register #(.width(32)) register_13 (.D(multiplexer_24_out), .Q(register_13_q), .clk(Clock));  // open: en, clr
  Register #(.width(32)) register_14 (.D(multiplexer_25_out), .Q(register_14_q), .clk(Clock));  // open: en, clr
  Comparator #(.width(5)) comparator_16 (.a(Read_Register_1), .b(5'b01110), .eq(comparator_16_eq));  // open: gt, lt
  Register #(.width(32)) register_15 (.D(multiplexer_27_out), .Q(s0_Value), .clk(Clock));  // open: en, clr
  Register #(.width(32)) register_16 (.D(multiplexer_28_out), .Q(s2_Value), .clk(Clock));  // open: en, clr
  Comparator #(.width(5)) comparator_17 (.a(Read_Register_1), .b(5'b10100), .eq(comparator_17_eq));  // open: gt, lt
  Comparator #(.width(5)) comparator_18 (.a(Read_Register_1), .b(5'b10110), .eq(comparator_18_eq));  // open: gt, lt
  Comparator #(.width(5)) comparator_19 (.a(Read_Register_1), .b(5'b11100), .eq(comparator_19_eq));  // open: gt, lt
  Comparator #(.width(5)) comparator_20 (.a(Read_Register_1), .b(5'b11110), .eq(comparator_20_eq));  // open: gt, lt
  Comparator #(.width(5)) comparator_21 (.a(Read_Register_1), .b({5{1'b0}}), .eq(comparator_21_eq));  // open: gt, lt
  Comparator #(.width(5)) comparator_22 (.a(Read_Register_1), .b(5'b00010), .eq(comparator_22_eq));  // open: gt, lt
  Comparator #(.width(5)) comparator_23 (.a(Read_Register_1), .b(5'b00100), .eq(comparator_23_eq));  // open: gt, lt
  Comparator #(.width(5)) comparator_24 (.a(Read_Register_1), .b(5'b00110), .eq(comparator_24_eq));  // open: gt, lt
  Comparator #(.width(5)) comparator_25 (.a(Read_Register_1), .b(5'b01000), .eq(comparator_25_eq));  // open: gt, lt
  Comparator #(.width(5)) comparator_26 (.a(Read_Register_1), .b(5'b01010), .eq(comparator_26_eq));  // open: gt, lt
  Comparator #(.width(5)) comparator_27 (.a(Read_Register_1), .b(5'b01100), .eq(comparator_27_eq));  // open: gt, lt
  Multiplexer #(.width(32), .enable("false")) multiplexer_31 (
    .in1(register_1_q), .out(Read_Data_1), .sel(comparator_27_eq));  // open: in0
  Multiplexer #(.width(32), .enable("false")) multiplexer_32 (
    .in1(register_1_q), .out(Read_Data_2), .sel(comparator_39_eq));  // open: in0
  Multiplexer #(.width(32), .enable("false")) multiplexer_33 (
    .in1(register_2_q), .out(Read_Data_1), .sel(comparator_16_eq));  // open: in0
  Multiplexer #(.width(32), .enable("false")) multiplexer_34 (
    .in1(register_2_q), .out(Read_Data_2), .sel(comparator_40_eq));  // open: in0
  Comparator #(.width(5)) comparator_28 (.a(Read_Register_1), .b(5'b10000), .eq(comparator_28_eq));  // open: gt, lt
  Comparator #(.width(5)) comparator_29 (.a(Read_Register_1), .b(5'b10010), .eq(comparator_29_eq));  // open: gt, lt
  Multiplexer #(.width(32), .enable("false")) multiplexer_35 (
    .in1(register_3_q), .out(Read_Data_1), .sel(comparator_17_eq));  // open: in0
  Multiplexer #(.width(32), .enable("false")) multiplexer_36 (
    .in1(register_3_q), .out(Read_Data_2), .sel(comparator_43_eq));  // open: in0
  Comparator #(.width(5)) comparator_30 (.a(Read_Register_2), .b(5'b10110), .eq(comparator_30_eq));  // open: gt, lt
  Multiplexer #(.width(32), .enable("false")) multiplexer_37 (
    .in1(register_4_q), .out(Read_Data_1), .sel(comparator_18_eq));  // open: in0
  Multiplexer #(.width(32), .enable("false")) multiplexer_38 (
    .in1(register_4_q), .out(Read_Data_2), .sel(comparator_30_eq));  // open: in0
  Comparator #(.width(5)) comparator_31 (.a(Read_Register_1), .b(5'b11000), .eq(comparator_31_eq));  // open: gt, lt
  Multiplexer #(.width(32), .enable("false")) multiplexer_39 (
    .in1(register_5_q), .out(Read_Data_1), .sel(comparator_31_eq));  // open: in0
  Multiplexer #(.width(32), .enable("false")) multiplexer_40 (
    .in1(register_5_q), .out(Read_Data_2), .sel(comparator_44_eq));  // open: in0
  Comparator #(.width(5)) comparator_32 (.a(Read_Register_1), .b(5'b11010), .eq(comparator_32_eq));  // open: gt, lt
  Multiplexer #(.width(32), .enable("false")) multiplexer_41 (
    .in1(register_6_q), .out(Read_Data_1), .sel(comparator_32_eq));  // open: in0
  Multiplexer #(.width(32), .enable("false")) multiplexer_42 (
    .in1(register_6_q), .out(Read_Data_2), .sel(comparator_45_eq));  // open: in0
  Comparator #(.width(5)) comparator_33 (.a(Read_Register_2), .b(5'b11100), .eq(comparator_33_eq));  // open: gt, lt
  Multiplexer #(.width(32), .enable("false")) multiplexer_43 (
    .in1(register_7_q), .out(Read_Data_1), .sel(comparator_19_eq));  // open: in0
  Multiplexer #(.width(32), .enable("false")) multiplexer_44 (
    .in1(register_7_q), .out(Read_Data_2), .sel(comparator_33_eq));  // open: in0
  Multiplexer #(.width(32), .enable("false")) multiplexer_45 (
    .in1(register_8_q), .out(Read_Data_1), .sel(comparator_20_eq));  // open: in0
  Multiplexer #(.width(32), .enable("false")) multiplexer_46 (
    .in1(register_8_q), .out(Read_Data_2), .sel(comparator_46_eq));  // open: in0
  Multiplexer #(.width(32), .enable("false")) multiplexer_47 (
    .in1(register_9_q), .out(Read_Data_1), .sel(comparator_21_eq));  // open: in0
  Multiplexer #(.width(32), .enable("false")) multiplexer_48 (
    .in1(register_9_q), .out(Read_Data_2), .sel(comparator_47_eq));  // open: in0
  Comparator #(.width(5)) comparator_34 (.a(Read_Register_2), .b(5'b00010), .eq(comparator_34_eq));  // open: gt, lt
  Multiplexer #(.width(32), .enable("false")) multiplexer_49 (
    .in1(register_10_q), .out(Read_Data_1), .sel(comparator_22_eq));  // open: in0
  Multiplexer #(.width(32), .enable("false")) multiplexer_50 (
    .in1(register_10_q), .out(Read_Data_2), .sel(comparator_34_eq));  // open: in0
  Comparator #(.width(5)) comparator_35 (.a(Read_Register_2), .b(5'b00100), .eq(comparator_35_eq));  // open: gt, lt
  Multiplexer #(.width(32), .enable("false")) multiplexer_51 (
    .in1(register_11_q), .out(Read_Data_1), .sel(comparator_23_eq));  // open: in0
  Multiplexer #(.width(32), .enable("false")) multiplexer_52 (
    .in1(register_11_q), .out(Read_Data_2), .sel(comparator_35_eq));  // open: in0
  Comparator #(.width(5)) comparator_36 (.a(Read_Register_2), .b(5'b00110), .eq(comparator_36_eq));  // open: gt, lt
  Multiplexer #(.width(32), .enable("false")) multiplexer_53 (
    .in1(register_12_q), .out(Read_Data_1), .sel(comparator_24_eq));  // open: in0
  Multiplexer #(.width(32), .enable("false")) multiplexer_54 (
    .in1(register_12_q), .out(Read_Data_2), .sel(comparator_36_eq));  // open: in0
  Comparator #(.width(5)) comparator_37 (.a(Read_Register_2), .b(5'b01000), .eq(comparator_37_eq));  // open: gt, lt
  Multiplexer #(.width(32), .enable("false")) multiplexer_55 (
    .in1(register_13_q), .out(Read_Data_1), .sel(comparator_25_eq));  // open: in0
  Multiplexer #(.width(32), .enable("false")) multiplexer_56 (
    .in1(register_13_q), .out(Read_Data_2), .sel(comparator_37_eq));  // open: in0
  Comparator #(.width(5)) comparator_38 (.a(Read_Register_2), .b(5'b01010), .eq(comparator_38_eq));  // open: gt, lt
  Multiplexer #(.width(32), .enable("false")) multiplexer_57 (
    .in1(register_14_q), .out(Read_Data_1), .sel(comparator_26_eq));  // open: in0
  Multiplexer #(.width(32), .enable("false")) multiplexer_58 (
    .in1(register_14_q), .out(Read_Data_2), .sel(comparator_38_eq));  // open: in0
  Comparator #(.width(5)) comparator_39 (.a(Read_Register_2), .b(5'b01100), .eq(comparator_39_eq));  // open: gt, lt
  Comparator #(.width(5)) comparator_40 (.a(Read_Register_2), .b(5'b01110), .eq(comparator_40_eq));  // open: gt, lt
  Comparator #(.width(5)) comparator_41 (.a(Read_Register_2), .b(5'b10000), .eq(comparator_41_eq));  // open: gt, lt
  Multiplexer #(.width(32), .enable("false")) multiplexer_59 (
    .in1(s0_Value), .out(Read_Data_1), .sel(comparator_28_eq));  // open: in0
  Multiplexer #(.width(32), .enable("false")) multiplexer_60 (
    .in1(s0_Value), .out(Read_Data_2), .sel(comparator_41_eq));  // open: in0
  Comparator #(.width(5)) comparator_42 (.a(Read_Register_2), .b(5'b10010), .eq(comparator_42_eq));  // open: gt, lt
  Multiplexer #(.width(32), .enable("false")) multiplexer_61 (
    .in1(s2_Value), .out(Read_Data_1), .sel(comparator_29_eq));  // open: in0
  Multiplexer #(.width(32), .enable("false")) multiplexer_62 (
    .in1(s2_Value), .out(Read_Data_2), .sel(comparator_42_eq));  // open: in0
  Comparator #(.width(5)) comparator_43 (.a(Read_Register_2), .b(5'b10100), .eq(comparator_43_eq));  // open: gt, lt
  Comparator #(.width(5)) comparator_44 (.a(Read_Register_2), .b(5'b11000), .eq(comparator_44_eq));  // open: gt, lt
  Comparator #(.width(5)) comparator_45 (.a(Read_Register_2), .b(5'b11010), .eq(comparator_45_eq));  // open: gt, lt
  Comparator #(.width(5)) comparator_46 (.a(Read_Register_2), .b(5'b11110), .eq(comparator_46_eq));  // open: gt, lt
  Comparator #(.width(5)) comparator_47 (.a(Read_Register_2), .b({5{1'b0}}), .eq(comparator_47_eq));  // open: gt, lt
  Multiplexer #(.width(5), .enable("false")) multiplexer_63 (
    .in1(Write_Register), .out(multiplexer_63_out), .sel(Write_Enable));  // open: in0
  Multiplexer #(.width(5), .enable("false")) multiplexer_64 (
    .in1(Write_Register), .out(multiplexer_64_out), .sel(Write_Enable));  // open: in0
  Multiplexer #(.width(5), .enable("false")) multiplexer_65 (
    .in1(Write_Register), .out(multiplexer_65_out), .sel(Write_Enable));  // open: in0
  Multiplexer #(.width(5), .enable("false")) multiplexer_66 (
    .in1(Write_Register), .out(multiplexer_66_out), .sel(Write_Enable));  // open: in0
  Multiplexer #(.width(5), .enable("false")) multiplexer_67 (
    .in1(Write_Register), .out(multiplexer_67_out), .sel(Write_Enable));  // open: in0
  Multiplexer #(.width(5), .enable("false")) multiplexer_68 (
    .in1(Write_Register), .out(multiplexer_68_out), .sel(Write_Enable));  // open: in0
  Multiplexer #(.width(5), .enable("false")) multiplexer_69 (
    .in1(Write_Register), .out(multiplexer_69_out), .sel(Write_Enable));  // open: in0
  Multiplexer #(.width(5), .enable("false")) multiplexer_70 (
    .in1(Write_Register), .out(multiplexer_70_out), .sel(Write_Enable));  // open: in0
  Multiplexer #(.width(5), .enable("false")) multiplexer_71 (
    .in1(Write_Register), .out(multiplexer_71_out), .sel(Write_Enable));  // open: in0
  Multiplexer #(.width(5), .enable("false")) multiplexer_72 (
    .in1(Write_Register), .out(multiplexer_72_out), .sel(Write_Enable));  // open: in0
  Multiplexer #(.width(5), .enable("false")) multiplexer_73 (
    .in1(Write_Register), .out(multiplexer_73_out), .sel(Write_Enable));  // open: in0
  Multiplexer #(.width(5), .enable("false")) multiplexer_74 (
    .in1(Write_Register), .out(multiplexer_74_out), .sel(Write_Enable));  // open: in0
  Multiplexer #(.width(5), .enable("false")) multiplexer_75 (
    .in1(Write_Register), .out(multiplexer_75_out), .sel(Write_Enable));  // open: in0
  Multiplexer #(.width(5), .enable("false")) multiplexer_76 (
    .in1(Write_Register), .out(multiplexer_76_out), .sel(Write_Enable));  // open: in0
  Multiplexer #(.width(5), .enable("false")) multiplexer_77 (
    .in1(Write_Register), .out(multiplexer_77_out), .sel(Write_Enable));  // open: in0
  Multiplexer #(.width(5), .enable("false")) multiplexer_78 (
    .in1(Write_Register), .out(multiplexer_78_out), .sel(Write_Enable));  // open: in0
  Comparator #(.width(5)) comparator_48 (.a(5'b00101), .b(multiplexer_63_out), .eq(comparator_48_eq));  // open: gt, lt
  Comparator #(.width(5)) comparator_49 (.a(5'b00111), .b(multiplexer_64_out), .eq(comparator_49_eq));  // open: gt, lt
  Multiplexer #(.width(32), .enable("false")) multiplexer_79 (
    .in1(Write_Data), .out(multiplexer_79_out), .sel(comparator_50_eq));  // open: in0
  Comparator #(.width(5)) comparator_50 (.a(5'b01001), .b(multiplexer_65_out), .eq(comparator_50_eq));  // open: gt, lt
  Multiplexer #(.width(32), .enable("false")) multiplexer_80 (
    .in1(Write_Data), .out(multiplexer_80_out), .sel(comparator_51_eq));  // open: in0
  Comparator #(.width(5)) comparator_51 (.a(5'b01011), .b(multiplexer_66_out), .eq(comparator_51_eq));  // open: gt, lt
  Multiplexer #(.width(32), .enable("false")) multiplexer_81 (
    .in1(Write_Data), .out(multiplexer_81_out), .sel(comparator_52_eq));  // open: in0
  Comparator #(.width(5)) comparator_52 (.a(5'b01101), .b(multiplexer_67_out), .eq(comparator_52_eq));  // open: gt, lt
  Multiplexer #(.width(32), .enable("false")) multiplexer_82 (
    .in1(Write_Data), .out(multiplexer_82_out), .sel(comparator_53_eq));  // open: in0
  Comparator #(.width(5)) comparator_53 (.a(5'b01111), .b(multiplexer_68_out), .eq(comparator_53_eq));  // open: gt, lt
  Multiplexer #(.width(32), .enable("false")) multiplexer_83 (
    .in1(Write_Data), .out(multiplexer_83_out), .sel(comparator_54_eq));  // open: in0
  Comparator #(.width(5)) comparator_54 (.a(5'b10001), .b(multiplexer_69_out), .eq(comparator_54_eq));  // open: gt, lt
  Multiplexer #(.width(32), .enable("false")) multiplexer_84 (
    .in1(Write_Data), .out(multiplexer_84_out), .sel(comparator_55_eq));  // open: in0
  Comparator #(.width(5)) comparator_55 (.a(5'b10011), .b(multiplexer_70_out), .eq(comparator_55_eq));  // open: gt, lt
  Multiplexer #(.width(32), .enable("false")) multiplexer_85 (
    .in1(Write_Data), .out(multiplexer_85_out), .sel(comparator_56_eq));  // open: in0
  Comparator #(.width(5)) comparator_56 (.a(5'b10101), .b(multiplexer_71_out), .eq(comparator_56_eq));  // open: gt, lt
  Multiplexer #(.width(32), .enable("false")) multiplexer_86 (
    .in1(Write_Data), .out(multiplexer_86_out), .sel(comparator_57_eq));  // open: in0
  Comparator #(.width(5)) comparator_57 (.a(5'b10111), .b(multiplexer_72_out), .eq(comparator_57_eq));  // open: gt, lt
  Multiplexer #(.width(32), .enable("false")) multiplexer_87 (
    .in1(Write_Data), .out(multiplexer_87_out), .sel(comparator_58_eq));  // open: in0
  Comparator #(.width(5)) comparator_58 (.a(5'b11001), .b(multiplexer_73_out), .eq(comparator_58_eq));  // open: gt, lt
  Multiplexer #(.width(32), .enable("false")) multiplexer_88 (
    .in1(Write_Data), .out(multiplexer_88_out), .sel(comparator_59_eq));  // open: in0
  Comparator #(.width(5)) comparator_59 (.a(5'b11011), .b(multiplexer_74_out), .eq(comparator_59_eq));  // open: gt, lt
  Multiplexer #(.width(32), .enable("false")) multiplexer_89 (
    .in1(Write_Data), .out(multiplexer_89_out), .sel(comparator_60_eq));  // open: in0
  Comparator #(.width(5)) comparator_60 (.a(5'b11101), .b(multiplexer_75_out), .eq(comparator_60_eq));  // open: gt, lt
  Multiplexer #(.width(32), .enable("false")) multiplexer_90 (
    .in1(Write_Data), .out(multiplexer_90_out), .sel(comparator_61_eq));  // open: in0
  Comparator #(.width(5)) comparator_61 (.a({5{1'b1}}), .b(multiplexer_76_out), .eq(comparator_61_eq));  // open: gt, lt
  Multiplexer #(.width(32), .enable("false")) multiplexer_91 (
    .in1(Write_Data), .out(multiplexer_91_out), .sel(comparator_62_eq));  // open: in0
  Comparator #(.width(5)) comparator_62 (.a(5'b00001), .b(multiplexer_77_out), .eq(comparator_62_eq));  // open: gt, lt
  Multiplexer #(.width(32), .enable("false")) multiplexer_92 (
    .in1(Write_Data), .out(multiplexer_92_out), .sel(comparator_63_eq));  // open: in0
  Comparator #(.width(5)) comparator_63 (.a(5'b00011), .b(multiplexer_78_out), .eq(comparator_63_eq));  // open: gt, lt
  Multiplexer #(.width(32), .enable("false")) multiplexer_93 (
    .in1(Write_Data), .out(multiplexer_93_out), .sel(comparator_48_eq));  // open: in0
  Multiplexer #(.width(32), .enable("false")) multiplexer_94 (
    .in1(Write_Data), .out(multiplexer_94_out), .sel(comparator_49_eq));  // open: in0
  Register #(.width(32)) register_17 (.D(multiplexer_79_out), .Q(register_17_q), .clk(Clock));  // open: en, clr
  Register #(.width(32)) register_18 (.D(multiplexer_80_out), .Q(register_18_q), .clk(Clock));  // open: en, clr
  Register #(.width(32)) register_19 (.D(multiplexer_81_out), .Q(register_19_q), .clk(Clock));  // open: en, clr
  Register #(.width(32)) register_20 (.D(multiplexer_82_out), .Q(register_20_q), .clk(Clock));  // open: en, clr
  Register #(.width(32)) register_21 (.D(multiplexer_83_out), .Q(s1_Value), .clk(Clock));  // open: en, clr
  Register #(.width(32)) register_22 (.D(multiplexer_84_out), .Q(register_22_q), .clk(Clock));  // open: en, clr
  Register #(.width(32)) register_23 (.D(multiplexer_85_out), .Q(register_23_q), .clk(Clock));  // open: en, clr
  Register #(.width(32)) register_24 (.D(multiplexer_86_out), .Q(register_24_q), .clk(Clock));  // open: en, clr
  Register #(.width(32)) register_25 (.D(multiplexer_87_out), .Q(register_25_q), .clk(Clock));  // open: en, clr
  Register #(.width(32)) register_26 (.D(multiplexer_88_out), .Q(register_26_q), .clk(Clock));  // open: en, clr
  Register #(.width(32)) register_27 (.D(multiplexer_89_out), .Q(sp_Value), .clk(Clock));  // open: en, clr
  Register #(.width(32)) register_28 (.D(multiplexer_90_out), .Q(ra_Value), .clk(Clock));  // open: en, clr
  Register #(.width(32)) register_29 (.D(multiplexer_91_out), .Q(register_29_q), .clk(Clock));  // open: en, clr
  Register #(.width(32)) register_30 (.D(multiplexer_92_out), .Q(register_30_q), .clk(Clock));  // open: en, clr
  Register #(.width(32)) register_31 (.D(multiplexer_93_out), .Q(register_31_q), .clk(Clock));  // open: en, clr
  Register #(.width(32)) register_32 (.D(multiplexer_94_out), .Q(register_32_q), .clk(Clock));  // open: en, clr
  Comparator #(.width(5)) comparator_64 (.a(Read_Register_1), .b(5'b01001), .eq(comparator_64_eq));  // open: gt, lt
  Comparator #(.width(5)) comparator_65 (.a(Read_Register_1), .b(5'b01011), .eq(comparator_65_eq));  // open: gt, lt
  Comparator #(.width(5)) comparator_66 (.a(Read_Register_1), .b(5'b01101), .eq(comparator_66_eq));  // open: gt, lt
  Comparator #(.width(5)) comparator_67 (.a(Read_Register_1), .b(5'b01111), .eq(comparator_67_eq));  // open: gt, lt
  Comparator #(.width(5)) comparator_68 (.a(Read_Register_1), .b(5'b10001), .eq(comparator_68_eq));  // open: gt, lt
  Comparator #(.width(5)) comparator_69 (.a(Read_Register_1), .b(5'b10011), .eq(comparator_69_eq));  // open: gt, lt
  Comparator #(.width(5)) comparator_70 (.a(Read_Register_1), .b(5'b10101), .eq(comparator_70_eq));  // open: gt, lt
  Comparator #(.width(5)) comparator_71 (.a(Read_Register_1), .b(5'b10111), .eq(comparator_71_eq));  // open: gt, lt
  Comparator #(.width(5)) comparator_72 (.a(Read_Register_1), .b(5'b11001), .eq(comparator_72_eq));  // open: gt, lt
  Comparator #(.width(5)) comparator_73 (.a(Read_Register_1), .b(5'b11011), .eq(comparator_73_eq));  // open: gt, lt
  Comparator #(.width(5)) comparator_74 (.a(Read_Register_1), .b(5'b11101), .eq(comparator_74_eq));  // open: gt, lt
  Comparator #(.width(5)) comparator_75 (.a(Read_Register_1), .b({5{1'b1}}), .eq(comparator_75_eq));  // open: gt, lt
  Comparator #(.width(5)) comparator_76 (.a(Read_Register_1), .b(5'b00001), .eq(comparator_76_eq));  // open: gt, lt
  Comparator #(.width(5)) comparator_77 (.a(Read_Register_1), .b(5'b00011), .eq(comparator_77_eq));  // open: gt, lt
  Comparator #(.width(5)) comparator_78 (.a(Read_Register_1), .b(5'b00101), .eq(comparator_78_eq));  // open: gt, lt
  Comparator #(.width(5)) comparator_79 (.a(Read_Register_1), .b(5'b00111), .eq(comparator_79_eq));  // open: gt, lt
  Multiplexer #(.width(32), .enable("false")) multiplexer_95 (
    .in1(register_17_q), .out(Read_Data_1), .sel(comparator_64_eq));  // open: in0
  Multiplexer #(.width(32), .enable("false")) multiplexer_96 (
    .in1(register_17_q), .out(Read_Data_2), .sel(comparator_92_eq));  // open: in0
  Multiplexer #(.width(32), .enable("false")) multiplexer_97 (
    .in1(register_18_q), .out(Read_Data_1), .sel(comparator_65_eq));  // open: in0
  Multiplexer #(.width(32), .enable("false")) multiplexer_98 (
    .in1(register_18_q), .out(Read_Data_2), .sel(comparator_93_eq));  // open: in0
  Comparator #(.width(5)) comparator_80 (.a(Read_Register_2), .b(5'b01101), .eq(comparator_80_eq));  // open: gt, lt
  Multiplexer #(.width(32), .enable("false")) multiplexer_99 (
    .in1(register_19_q), .out(Read_Data_1), .sel(comparator_66_eq));  // open: in0
  Multiplexer #(.width(32), .enable("false")) multiplexer_100 (
    .in1(register_19_q), .out(Read_Data_2), .sel(comparator_80_eq));  // open: in0
  Comparator #(.width(5)) comparator_81 (.a(Read_Register_2), .b(5'b01111), .eq(comparator_81_eq));  // open: gt, lt
  Multiplexer #(.width(32), .enable("false")) multiplexer_101 (
    .in1(register_20_q), .out(Read_Data_1), .sel(comparator_67_eq));  // open: in0
  Multiplexer #(.width(32), .enable("false")) multiplexer_102 (
    .in1(register_20_q), .out(Read_Data_2), .sel(comparator_81_eq));  // open: in0
  Multiplexer #(.width(32), .enable("false")) multiplexer_103 (
    .in1(s1_Value), .out(Read_Data_1), .sel(comparator_68_eq));  // open: in0
  Multiplexer #(.width(32), .enable("false")) multiplexer_104 (
    .in1(s1_Value), .out(Read_Data_2), .sel(comparator_94_eq));  // open: in0
  Multiplexer #(.width(32), .enable("false")) multiplexer_105 (
    .in1(register_22_q), .out(Read_Data_1), .sel(comparator_69_eq));  // open: in0
  Multiplexer #(.width(32), .enable("false")) multiplexer_106 (
    .in1(register_22_q), .out(Read_Data_2), .sel(comparator_95_eq));  // open: in0
  Comparator #(.width(5)) comparator_82 (.a(Read_Register_2), .b(5'b10101), .eq(comparator_82_eq));  // open: gt, lt
  Multiplexer #(.width(32), .enable("false")) multiplexer_107 (
    .in1(register_23_q), .out(Read_Data_1), .sel(comparator_70_eq));  // open: in0
  Multiplexer #(.width(32), .enable("false")) multiplexer_108 (
    .in1(register_23_q), .out(Read_Data_2), .sel(comparator_82_eq));  // open: in0
  Comparator #(.width(5)) comparator_83 (.a(Read_Register_2), .b(5'b10111), .eq(comparator_83_eq));  // open: gt, lt
  Multiplexer #(.width(32), .enable("false")) multiplexer_109 (
    .in1(register_24_q), .out(Read_Data_1), .sel(comparator_71_eq));  // open: in0
  Multiplexer #(.width(32), .enable("false")) multiplexer_110 (
    .in1(register_24_q), .out(Read_Data_2), .sel(comparator_83_eq));  // open: in0
  Comparator #(.width(5)) comparator_84 (.a(Read_Register_2), .b(5'b11001), .eq(comparator_84_eq));  // open: gt, lt
  Multiplexer #(.width(32), .enable("false")) multiplexer_111 (
    .in1(register_25_q), .out(Read_Data_1), .sel(comparator_72_eq));  // open: in0
  Multiplexer #(.width(32), .enable("false")) multiplexer_112 (
    .in1(register_25_q), .out(Read_Data_2), .sel(comparator_84_eq));  // open: in0
  Comparator #(.width(5)) comparator_85 (.a(Read_Register_2), .b(5'b11011), .eq(comparator_85_eq));  // open: gt, lt
  Multiplexer #(.width(32), .enable("false")) multiplexer_113 (
    .in1(register_26_q), .out(Read_Data_1), .sel(comparator_73_eq));  // open: in0
  Multiplexer #(.width(32), .enable("false")) multiplexer_114 (
    .in1(register_26_q), .out(Read_Data_2), .sel(comparator_85_eq));  // open: in0
  Comparator #(.width(5)) comparator_86 (.a(Read_Register_2), .b(5'b11101), .eq(comparator_86_eq));  // open: gt, lt
  Multiplexer #(.width(32), .enable("false")) multiplexer_115 (
    .in1(sp_Value), .out(Read_Data_1), .sel(comparator_74_eq));  // open: in0
  Multiplexer #(.width(32), .enable("false")) multiplexer_116 (
    .in1(sp_Value), .out(Read_Data_2), .sel(comparator_86_eq));  // open: in0
  Comparator #(.width(5)) comparator_87 (.a(Read_Register_2), .b({5{1'b1}}), .eq(comparator_87_eq));  // open: gt, lt
  Multiplexer #(.width(32), .enable("false")) multiplexer_117 (
    .in1(ra_Value), .out(Read_Data_1), .sel(comparator_75_eq));  // open: in0
  Multiplexer #(.width(32), .enable("false")) multiplexer_118 (
    .in1(ra_Value), .out(Read_Data_2), .sel(comparator_87_eq));  // open: in0
  Comparator #(.width(5)) comparator_88 (.a(Read_Register_2), .b(5'b00001), .eq(comparator_88_eq));  // open: gt, lt
  Multiplexer #(.width(32), .enable("false")) multiplexer_119 (
    .in1(register_29_q), .out(Read_Data_1), .sel(comparator_76_eq));  // open: in0
  Multiplexer #(.width(32), .enable("false")) multiplexer_120 (
    .in1(register_29_q), .out(Read_Data_2), .sel(comparator_88_eq));  // open: in0
  Comparator #(.width(5)) comparator_89 (.a(Read_Register_2), .b(5'b00011), .eq(comparator_89_eq));  // open: gt, lt
  Multiplexer #(.width(32), .enable("false")) multiplexer_121 (
    .in1(register_30_q), .out(Read_Data_1), .sel(comparator_77_eq));  // open: in0
  Multiplexer #(.width(32), .enable("false")) multiplexer_122 (
    .in1(register_30_q), .out(Read_Data_2), .sel(comparator_89_eq));  // open: in0
  Comparator #(.width(5)) comparator_90 (.a(Read_Register_2), .b(5'b00101), .eq(comparator_90_eq));  // open: gt, lt
  Multiplexer #(.width(32), .enable("false")) multiplexer_123 (
    .in1(register_31_q), .out(Read_Data_1), .sel(comparator_78_eq));  // open: in0
  Multiplexer #(.width(32), .enable("false")) multiplexer_124 (
    .in1(register_31_q), .out(Read_Data_2), .sel(comparator_90_eq));  // open: in0
  Comparator #(.width(5)) comparator_91 (.a(Read_Register_2), .b(5'b00111), .eq(comparator_91_eq));  // open: gt, lt
  Multiplexer #(.width(32), .enable("false")) multiplexer_125 (
    .in1(register_32_q), .out(Read_Data_1), .sel(comparator_79_eq));  // open: in0
  Multiplexer #(.width(32), .enable("false")) multiplexer_126 (
    .in1(register_32_q), .out(Read_Data_2), .sel(comparator_91_eq));  // open: in0
  Comparator #(.width(5)) comparator_92 (.a(Read_Register_2), .b(5'b01001), .eq(comparator_92_eq));  // open: gt, lt
  Comparator #(.width(5)) comparator_93 (.a(Read_Register_2), .b(5'b01011), .eq(comparator_93_eq));  // open: gt, lt
  Comparator #(.width(5)) comparator_94 (.a(Read_Register_2), .b(5'b10001), .eq(comparator_94_eq));  // open: gt, lt
  Comparator #(.width(5)) comparator_95 (.a(Read_Register_2), .b(5'b10011), .eq(comparator_95_eq));  // open: gt, lt

  // Other names for the same wires on the sheet: _16[31:0] = s0_Value; _17[31:0] = s1_Value; _18[31:0] = s2_Value;
  //   _29[31:0] = sp_Value; _31[31:0] = ra_Value; clk = Clock; read_data1[31:0] = Read_Data_1;
  //   read_data2[31:0] = Read_Data_2; read_reg1[4:0] = Read_Register_1; read_reg2[4:0] = Read_Register_2;
  //   write_en = Write_Enable; write_reg[4:0] = Write_Register

  // Notes on the sheet:
  //   INPUTS to your circuit
  //   DON'T CHANGE THE LOCATIONS OF THE INPUTS AND OUTPUTS!
  //   These are DEBUG/TEST outputs from your circuit.
  //   OUTPUTS from your circuit
endmodule
